# Fritzing sketch Pinscape Pico Lite (saved by Fritzing 1.0.5)
circuit board: 7.6cm x 6.2cm
breadboards: 1

parts:
  J1 = female pin header, 2 pins [form="♀ (female)"]
  J2 = female pin header, 2 pins [form="♀ (female)"]
  J4 = female pin header, 4 pins [form="♀ (female)"]
  J6 = female pin header, 4 pins [form="♀ (female)"]
  J7 = female pin header, 3 pins [form="♀ (female)"]
  J8 = female pin header, 2 pins [form="♀ (female)"]
  J5 = female pin header, 4 pins [form="♀ (female)"]
  J11 = female pin header, 2 pins [form="♀ (female)"]
  MMA8451 = Adafruit MMA8451 Accelerometer [part_number="Adafruit #2019"]
  J13 = female pin header, 20 pins [form="♀ (female)"]
  J12 = female pin header, 20 pins [form="♀ (female)"]
  Adafruit#1 = Adafruit ADS1115 16-Bit ADC without SMD [part_number=1085]
  J14 = female pin header, 2 pins [form="♀ (female)"]
  R1 = Resistor [tolerance=±5% power=0.25W resistance=10 package=THT]
  R2 = Resistor [tolerance=±5% power=0.25W resistance=10 package=THT]
  J15 = female pin header, 2 pins [form="♀ (female)"]
  J16 = female pin header, 2 pins [form="♀ (female)"]
  J17 = female pin header, 2 pins [form="♀ (female)"]
  J18 = female pin header, 2 pins [form="♀ (female)"]

nets:
  N1: J1.pin1, J13.pin1
  N2: J1.pin2, J13.pin2
  N3: J2.pin1, J13.pin4
  N4: J2.pin2, J13.pin5
  N5: J4.pin1, J13.pin9
  N6: J4.pin2, J13.pin10
  N7: J4.pin3, J13.pin11
  N8: J4.pin4, J13.pin12
  N9: J6.pin1, J12.pin12
  N10: J6.pin2, J12.pin14
  N11: J6.pin3, J12.pin15
  N12: J6.pin4, J12.pin16
  N13: J7.pin1, Adafruit#1.AVDD
  N14: J7.pin2, Adafruit#1.AIN0
  N15: J7.pin3, Adafruit#1.AGND
  N16: J8.pin1, J13.pin19
  N17: J8.pin2, J13.pin20
  N18: J5.pin1, J13.pin14
  N19: J5.pin2, J13.pin15
  N20: J5.pin3, J13.pin16
  N21: J5.pin4, J13.pin17
  N22: J11.pin1, J12.pin19
  N23: J11.pin2, J12.pin20
  N24: MMA8451.SDA, J12.pin10, Adafruit#1.SDA
  N25: MMA8451.SCL, J12.pin9, Adafruit#1.SCL
  N26: MMA8451.INT1, J12.pin7
  +3V3: MMA8451.+3V3, J12.pin5, Adafruit#1.VCC, R1.Pin_0
  N27: MMA8451.GND, J15.pin1, J15.pin2, J16.pin1, J16.pin2, J17.pin1, J17.pin2, J18.pin1, J18.pin2
  N28: J13.pin6, J14.pin1
  N29: J13.pin7, J14.pin2
  N30: J12.pin17, Adafruit#1.ALERT
  N31: Adafruit#1.AIN3, R1.Pin_1, R2.Pin_0

notes:
  left
  right
  magna
  start
  exit
  launch
  buyin
  next
  cancel
  previous
  enter
  volume up
  volume down
  middle shute
  right shute
  coin door
  left shute
  control panel
  -
  slider
  +
  plunger
  Pinscape Pico Lite
  ground
  MMA8451
  ADS1115
  Raspberry Pi Pico H
  2
  1
  spare
  version 1
  flip
  2nd flip
  door
  vp
  front

custom parts:
  Adafruit MMA8451 Accelerometer: So many accelerometers and so little time! We've expanded our accelerometer selection even more with this high-precision and inexpensive MMA8451 Triple-Axis Accelerometer w/ 14-bit ADC. You can detect motion, tilt and basic orientation with a digital accelerometer - and the MMA8451 is a great accelerometer to start with. It has a wide usage range, from +-2g up to +-8g yet is easy to use with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
  Adafruit ADS1115 16-Bit ADC without SMD: For microcontrollers without an analog-to-digital converter or when you want a higher-precision ADC, the ADS1115 provides 16-bit precision at 860 samples/second over I2C. The chip can be configured as 4 single-ended input channels, or two differential channels. As a nice bonus, it even includes a programmable gain amplifier, up to x16, to help boost up smaller single/differential signals to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
